# Fritzing sketch fritzing (saved by Fritzing 0.9.3b)

parts:
  Componente1 = Arduino Uno (Rev3)  # not connected
  Componente2 = Arduino Board Ethernet
  GY2 = MPU-6050 Board GY-521 [form="♀ (female)" package=THT]

nets:
  N1: Componente2.A4, GY2.pin4
  N2: Componente2.A5, GY2.pin3
  N3: Componente2.3V3, GY2.pin1
  N4: Componente2.GND, GY2.pin2

custom parts:
  MPU-6050 Board GY-521: Acelerometro y Giroscopio MPU-6050 Board GY-521
